# Fritzing sketch button (saved by Fritzing 0.9.10b)
breadboards: 1

parts:
  Mod1 = Amica NodeMCU DEVKIT 1.0
  S1 = Pushbutton [package="[THT]"]
  R1 = Resistor [tolerance=±5% resistance=220 package="1206 [SMD]"]
  LED1 = smd LED [color="White (4500K)" package="0805 [SMD]"]

nets:
  N1: Mod1.pin1, Mod1.pin_10, Mod1.pin_26
  N2: Mod1.pin2, Mod1.pin_9, Mod1.pin_25, Mod1.pin_29, S1.Pin_1, S1.Pin_2, R1.Pin_1
  N3: Mod1.pin8, S1.Pin_3, S1.Pin_4
  N4: Mod1.pin_14, LED1.anode
  N5: R1.Pin_0, LED1.cathode
