# Fritzing sketch distance (saved by Fritzing 0.9.10b)
breadboards: 1

parts:
  Mod1 = Amica NodeMCU DEVKIT 1.0
  HC-SR04_Sensor_1 = HC-SR04 Ultrasonic Distance Sensor

nets:
  N1: Mod1.pin1, Mod1.pin_10, Mod1.pin_26, HC-SR04_Sensor_1.VCC
  N2: Mod1.pin2, Mod1.pin_9, Mod1.pin_25, Mod1.pin_29, HC-SR04_Sensor_1.GND
  N3: Mod1.pin7, HC-SR04_Sensor_1.TRIG
  N4: Mod1.pin8, HC-SR04_Sensor_1.ECHO

notes:
  D5 = GPIO14 (echo)
  D6 = GPIO12 (Trig)
