# Fritzing sketch lap_check (saved by Fritzing 0.9.10b)
breadboards: 1

parts:
  IR_Sensor = fc-51 [package=THT]
  Mod1 = Amica NodeMCU DEVKIT 1.0
  IR_Sensor1 = fc-51 [package=THT]

nets:
  N1: IR_Sensor.pin1, Mod1.pin_14
  N2: IR_Sensor.pin2, Mod1.pin2, Mod1.pin_9, Mod1.pin_25, Mod1.pin_29, IR_Sensor1.pin2
  N3: IR_Sensor.pin3, Mod1.pin1, Mod1.pin_10, Mod1.pin_26
  N4: Mod1.pin_13, IR_Sensor1.pin1
