# Fritzing sketch lights (saved by Fritzing 0.9.10b)
breadboards: 1

parts:
  Mod1 = Amica NodeMCU DEVKIT 1.0
  R1 = Resistor [tolerance=±5% resistance=220 package="1206 [SMD]"]
  LED1 = smd LED [color="Red (633nm)" package="0805 [SMD]"]
  LED2 = smd LED [color="Yellow (585nm)" package="0805 [SMD]"]
  LED3 = smd LED [color="Green (560nm)" package="0805 [SMD]"]

nets:
  N1: Mod1.pin1, Mod1.pin_10, Mod1.pin_26, R1.Pin_1
  N2: Mod1.pin2, Mod1.pin_9, Mod1.pin_25, Mod1.pin_29
  N3: Mod1.pin_12, LED1.anode
  N4: Mod1.pin_13, LED3.anode
  N5: Mod1.pin_14, LED2.anode
  N6: R1.Pin_0, LED1.cathode, LED2.cathode, LED3.cathode
