# Fritzing sketch overheat (saved by Fritzing 0.9.10b)
breadboards: 1

parts:
  Mod1 = Amica NodeMCU DEVKIT 1.0
  DS1 = DS18B20 1-Wire Temperature Sensor [part_number=DS18B20]
  R1 = Resistor [tolerance=±5% resistance=4700 package="0402 [SMD]"]

nets:
  N1: Mod1.pin1, Mod1.pin_10, Mod1.pin_26, DS1.VDD, R1.Pin_0
  N2: Mod1.pin2, Mod1.pin_9, Mod1.pin_25, Mod1.pin_29, DS1.GND
  N3: Mod1.pin_13, DS1.DQ, R1.Pin_1

notes:
  D2 = GPIO4
  4,7 KOhm
