# Fritzing sketch speed_actuator (saved by Fritzing 0.9.10b)
breadboards: 1

parts:
  U1 = 4077 4 x 2 Input XNOR Gate, single part [part_number=4077 package="DIP (Dual Inline) [THT]"]
  U3 = ESP32-38PinWide [part_number=ESP32-38PinWide]
  LED1 = smd LED [color="Blue (470nm)" package="0805 [SMD]"]
  R1 = Resistor [tolerance=±5% power=0.25 resistance=220 package=THT]

nets:
  GND: U1.GND, U3.GND, R1.Pin_0
  N1: U1.A3, U3.GPIO22
  N2: U1.B3, U3.GPIO21
  N3: U1.VDD, U3.3.3
  N4: U3.GPIO4, LED1.anode
  N5: LED1.cathode, R1.Pin_1

notes:
  Cyan - Pot 0 (H-W)
  Orange - Pot 1 (H-W)
  D22 - SCL
  D21 - SDA
  D4 - Signal LED

custom parts:
  ESP32-38PinWide: Generic 38-Pin ESP32 with wide format (only access to one side of pins on a breadboard) based on Stephen Lilley's HiLetgo ESP-WROOM-32 ESP32 ESP-32S Development Board.
